# Fritzing sketch save_shutdown_for_power_boost (saved by Fritzing 0.9.3b)
circuit board: 10cm x 6cm
breadboards: 1

parts:
  U1 = LIPO-1000mAh [package=lipo-1000]
  Q1 = MOSFET-NCHANNEL [package=sot323]
  C1 = Capacitor [package=0805]
  R1 = Resistor [tolerance=±5% resistance=1M package="0805 [SMD]"]
  R2 = Resistor [tolerance=±5% resistance=10k package="0805 [SMD]"]
  R3 = Resistor [tolerance=±5% resistance=10k package="0805 [SMD]"]
  R4 = Resistor [tolerance=±5% resistance=1k package="0805 [SMD]"]
  R5 = Resistor [tolerance=±5% resistance=1k package="0805 [SMD]"]
  Q2 = MOSFET-NCHANNEL [package=sot323]
  S1 = Toggle Switch [package=THT]
  Bauteil1 = Adafruit PowerBoost 1000C [part_number="Adafruit #2465"]

nets:
  N1: U1.+, R2.Pin_1, R3.Pin_1, S1.COM, Bauteil1.VLIPO
  N2: U1.-, Q1.S, C1.1, R1.Pin_0, Q2.S, Bauteil1.GND
  N3: Q1.G, R5.Pin_0
  N4: Q1.D, R3.Pin_0, R4.Pin_1
  N5: C1.2, R1.Pin_1, R5.Pin_1, S1.L2
  N6: R2.Pin_0, Q2.D, Bauteil1.ENABLE
  N7: R4.Pin_0, Q2.G

notes:
  22uF

custom parts:
  Adafruit PowerBoost 1000C: PowerBoost 1000C is the perfect power supply for your portable project! With a built-in load-sharing battery charger circuit, you'll be able to keep your power-hungry project running even while recharging the battery! This little DC/DC boost converter module can be powered by any 3.7V LiIon/LiPoly battery, and convert the battery output to 5.2V DC for running your 5V projects.
